# Fritzing sketch Anschluss_DS18B20 (saved by Fritzing 0.9.10b)
breadboards: 1

parts:
  Raspberry_Pi_1 = Raspberry Pi 3 [part_number=RPI-3-V1.2]
  DS1 = DS18B20 1-Wire Temperature Sensor [part_number=DS18B20]
  R1 = Resistor [tolerance=±5% power=0.25 resistance=4.7 package=THT]

nets:
  3V3: Raspberry_Pi_1.3v3, DS1.VDD, R1.Pin_1
  N1: Raspberry_Pi_1.GIPO21, DS1.DQ, R1.Pin_0
  GND: Raspberry_Pi_1.GND, DS1.GND
