# Fritzing sketch Anschluss_LED_Matrix (saved by Fritzing 0.9.10b)
breadboards: 1

parts:
  Raspberry_Pi_1 = Raspberry Pi 3 [part_number=RPI-3-V1.2]
  DS1 = DS18B20 1-Wire Temperature Sensor [part_number=DS18B20]
  R1 = Resistor [tolerance=±5% power=0.25 resistance=4.7 package=THT]
  Bauteil3 = Matrix LED de 8x8 basada en MAX7219
  Bauteil4 = Matrix LED de 8x8 basada en MAX7219
  S1 = Pushbutton [package="[SMD]"]

nets:
  3V3: Raspberry_Pi_1.3v3, DS1.VDD, R1.Pin_1
  N1: Raspberry_Pi_1.GIPO4, DS1.DQ, R1.Pin_0
  N2: Raspberry_Pi_1.GIPO17, S1.Pin_3, S1.Pin_4
  N3: Raspberry_Pi_1.GIPO10, Bauteil4.DOUT
  N4: Raspberry_Pi_1.GIPO11, Bauteil4.CLK(OUT)
  N5: Raspberry_Pi_1.GIPO8, Bauteil4.CS(OUT)
  GND: Raspberry_Pi_1.GND, DS1.GND, Bauteil4.GND#6, S1.Pin_1, S1.Pin_2
  N6: Raspberry_Pi_1.5V, Bauteil4.VCC(OUT)
  N7: Bauteil3.VCC(OUT), Bauteil4.VCC
  N8: Bauteil3.GND, Bauteil4.GND#1
  N9: Bauteil3.CS(OUT), Bauteil4.CS
  N10: Bauteil3.CLK(OUT), Bauteil4.CLK
  N11: Bauteil3.DOUT, Bauteil4.DIN
